# Fritzing sketch control (saved by Fritzing 0.9.10b)
breadboards: 1

parts:
  元件1 = NRF24L01+ Breakout Board
  元件2 = Thumb Joystick
  元件3 = Arduino Nano (Rev3.0)
  元件4 = Thumb Joystick
  R2 = Rotary Potentiometer (Large) [maximum_resistance=10kΩ knob_status=50% power=0.5W package=THT]
  R3 = Resistor [tolerance=±5% resistance=10k package="1206 [SMD]"]
  R4 = Resistor [tolerance=±5% resistance=10k package="1206 [SMD]"]
  C8 = Capacitor Polarized [package=panasonic_c]
  R1 = Rotary Potentiometer (Large) [maximum_resistance=10kΩ knob_status=75% power=0.5W package=THT]

nets:
  GND: 元件1.GND, 元件2.GND, 元件3.GND, 元件4.GND, R2.leg2, C8.-, R1.leg2
  VCC: 元件1.VCC, 元件3.3V3, C8.+
  N1: 元件1.CE, 元件3.D7
  N2: 元件1.SCK, 元件3.D13/SCK
  N3: 元件1.MOSI, 元件3.D11/MOSI
  N4: 元件1.MISO, 元件3.D12/MISO
  N5: 元件2.SEL, 元件3.D2, R4.Pin_0
  N6: 元件2.HORZ, 元件3.A1
  N7: 元件2.VERT, 元件3.A0
  VCC_2: 元件2.VCC, 元件3.5V, 元件4.VCC, R2.leg1, R3.Pin_1, R4.Pin_1, R1.leg1
  N8: 元件3.D3, 元件4.SEL, R3.Pin_0
  N9: 元件3.A5, R2.wiper
  N10: 元件3.A4, R1.wiper
  N11: 元件3.A3, 元件4.HORZ
  N12: 元件3.A2, 元件4.VERT
