# Fritzing sketch remote (saved by Fritzing 0.9.10b)
breadboards: 1

parts:
  M1 = Dagu DGServo 9g (Top view) [part_number=RS001B]
  M2 = Dagu DGServo 9g (Top view) [part_number=RS001B]
  M3 = Dagu DGServo 9g (Top view) [part_number=RS001B]
  M4 = Dagu DGServo 9g (Top view) [part_number=RS001B]
  M5 = Dagu DGServo 9g (Top view) [part_number=RS001B]
  元件1 = Arduino Nano (Rev3.0)
  元件2 = NRF24L01+ Breakout Board
  C7 = Capacitor Polarized [package=panasonic_c]
  J1 = Piezo Speaker
  LED1 = smd LED [color="Red (633nm)" package="0603 [SMD]"]
  R5 = Resistor [tolerance=±5% resistance=220 package="1206 [SMD]"]

nets:
  GND: M1.gnd, M2.gnd, M3.gnd, M4.gnd, M5.gnd, 元件1.GND, 元件2.GND, C7.-, J1.pin1, LED1.cathode
  VCC: M1.vcc, M2.vcc, M3.vcc, M4.vcc, M5.vcc, 元件1.5V
  N1: M1.pulse, 元件1.D2
  N2: M2.pulse, 元件1.D3
  N3: M3.pulse, 元件1.D4
  N4: M4.pulse, 元件1.D5
  N5: M5.pulse, 元件1.D6
  N6: 元件1.D7, 元件2.CE
  N7: 元件1.D8, 元件2.CS
  N8: 元件1.D11/MOSI, 元件2.MOSI
  N9: 元件1.D12/MISO, 元件2.MISO
  N10: 元件1.A1, R5.Pin_1
  N11: 元件1.A0, J1.pin2
  3V3: 元件1.3V3, 元件2.VCC, C7.+
  N12: 元件1.D13/SCK, 元件2.SCK
  N13: LED1.anode, R5.Pin_0
